# Fritzing sketch Sketch (saved by Fritzing 0.9.3b)
breadboards: 2

parts:
  tft1 = 3.2in tft touch screen  # not connected
  Part1 = Arduino Mega ADK (Rev3)
  Part2 = Arduino Nano (Rev3.0)
  Part3 = Bluetooth HC-05 Macho  # not connected
  LED1 = LED - 5mm [color="Red (633nm)" package="5 mm [THT]"]  # not connected
  R1 = Resistor [tolerance=±5% resistance=220 package=THT]
  S1 = Pushbutton [package="[THT]"]
  R2 = Resistor [tolerance=±5% resistance=10k package=THT]
  J1 = Piezo Speaker
  Q1 = NPN-Transistor [package="TO92 [THT]"]
  R3 = Resistor [tolerance=±5% resistance=1k package=THT]
  RTC1 = DS3231 AT24C32 Real Time Clock  # not connected
  Part4 = Bluetooth HC-05 Macho  # not connected

nets:
  N1: Part1.D13_PWM, S1.Pin_3, S1.Pin_4, R2.Pin_1
  N2: Part1.D8_PWM, R3.Pin_0
  N3: Part1.5V, R2.Pin_0
  N4: Part1.GND, S1.Pin_1, S1.Pin_2, Q1.E
  N5: Part2.GND, R1.Pin_1
  N6: J1.pin1, Q1.C
  N7: Q1.B, R3.Pin_1

notes:
  GOES ON TOP OF THE MEGA BOARD.

custom parts:
  3.2in tft touch screen: 3.2" tft touch screen lcd display
  DS3231 AT24C32 Real Time Clock: Real-time clock basedo on chip DS3231, plus memory chip AT24C32 (32 Kb storage capacity). On-chip temperature sensor with an accuracy of ±3 ℃, I2C bus interface maximum speed: 400 kHz. Operating voltage: 3.3 V to 5.5 V with battery backup capabilities.
